# Fritzing sketch WIRING DIAGRAM (saved by Fritzing 1.0.6)
breadboards: 1

parts:
  Mod1 = Amica NodeMCU DEVKIT 1.0
  STATION_START = TCRT5000 sensor module [part_number=151608]
  STATION_END = TCRT5000 sensor module [part_number=151608]
  TOMBOL_RESET_CONFIG = Round Pushbutton
  RESULT_GOOD = TCRT5000 sensor module [part_number=151608]
  RESULT_REJECT = TCRT5000 sensor module [part_number=151608]

nets:
  N1: Mod1.pin1, Mod1.pin_10, Mod1.pin_26
  N2: Mod1.pin2, Mod1.pin_9, Mod1.pin_25, Mod1.pin_29, STATION_START.T-, STATION_END.T-, TOMBOL_RESET_CONFIG.leg1, RESULT_GOOD.T-
  N3: Mod1.pin5, STATION_END.T+, RESULT_GOOD.T+, RESULT_REJECT.T+
  N4: Mod1.pin6, TOMBOL_RESET_CONFIG.leg0
  N5: Mod1.pin7, STATION_END.D+
  N6: Mod1.pin8, STATION_START.D+
  N7: Mod1.pin_13, RESULT_REJECT.D+
  N8: Mod1.pin_14, RESULT_GOOD.D+

notes:
  write your nte here]

custom parts:
  TCRT5000 sensor module: breakout board with TCRT5000
